# Fritzing sketch cablage-pro-micro (saved by Fritzing 1.0.1rc)

parts:
  Pro_Micro1 = Pro Micro
  S1 = Round Pushbutton
  PCB2 = PCB Détection v3 (OH37 + pull-up + JST-XH) [package="custom board"]
  PCB3 = PCB Détection v3 (OH37 + pull-up + JST-XH) [package="custom board"]
  PCB4 = PCB Détection v3 (OH37 + pull-up + JST-XH) [package="custom board"]

nets:
  N1: Pro_Micro1.GND#4, S1.leg1
  N2: Pro_Micro1.D7, S1.leg0
  N3: Pro_Micro1.D16/MOSI, PCB3.DATA
  N4: Pro_Micro1.D14/MISO, PCB2.DATA
  N5: Pro_Micro1.D15/SCLK, PCB4.DATA
  N6: Pro_Micro1.VCC, PCB2.+, PCB3.+, PCB4.+
  N7: PCB2.-, PCB3.-, PCB4.-

custom parts:
  Pro Micro: The SparkFun Pro Micro is a complete USB-based microcontoller development system, in a very small footprint, capable of implementing many types of projects. All programming can be done via the USB port.
  PCB Détection v3 (OH37 + pull-up + JST-XH): Carte de détection complète (pcb-detection-v3.fzz) représentée comme un seul composant : capteur à effet Hall OH37 (U1), résistance de tirage 10k (R1) entre les pistes + et DATA (la piste − passe tout droit sous R1 jusqu'au pin central du OH37), connecteur JST-XH 3 points (J1, +/-/DATA de gauche à droite vu de dessus). Sérigraphie « SMD_v3_Arducible ». La vue platine d'essai et la vue circuit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
