# Fritzing sketch pcb-detection-v3 (saved by Fritzing 1.0.1rc)
circuit board: 3.39999cm x 4.79999cm

parts:
  H1 = Mounting Hole H1 (4mm, detection PCB v3)  # not connected
  H2 = Mounting Hole H2 (3.9756mm, detection PCB v3)  # not connected
  R1 = 10K Resistor (0603, detection PCB v3) [Resistance=10k package="0603 [SMD]"]
  U1 = OH37 Hall-Effect Switch (SOT-23-3, detection PCB v3) [part_number=OH37 package=SOT-23-3]
  J1 = XH-3A Connector, DATA/-/+ (detection PCB v3) [package=CONN-TH_XH-3A]

nets:
  N1: R1.Pin_0, U1.2, J1.DATA
  N2: R1.Pin_1, U1.3, J1.+
  N3: U1.1, J1.-

custom parts:
  Mounting Hole H1 (4mm, detection PCB v3): Non-plated 4mm mounting hole on the target-detection PCB, exact copy of the circular cutout in Gerber_BoardOutlineLayer.GKO from gerber-pcb-detection-v3.zip. Custom static part used instead of Fritzing's built-in resizable "Hole" shape, whose instance placement uses legacy (non-mm) coordinates and was not reliable to author directly in XML.
  Mounting Hole H2 (3.9756mm, detection PCB v3): Non-plated 3.9756mm mounting hole on the target-detection PCB, exact copy of the circular cutout in Gerber_BoardOutlineLayer.GKO from gerber-pcb-detection-v3.zip. Custom static part used instead of Fritzing's built-in resizable "Hole" shape, whose instance placement uses legacy (non-mm) coordinates and was not reliable to author directly in XML.
  10K Resistor (0603, detection PCB v3): 10k pull-up resistor for the OH37 Hall-effect switch, designator "10K" on the target-detection PCB (bom-jlcpcb-v3.csv / LCSC C3017715). PCB footprint pads are an exact copy of the Gerber_TopLayer.GTL flashes from gerber-pcb-detection-v3.zip (0.8065mm x 0.864mm pads, 1.5065mm pitch).
  OH37 Hall-Effect Switch (SOT-23-3, detection PCB v3): Nanjing Ouzhuo Tech OH37 Hall-effect switch, designator "OH37" on the target-detection PCB (bom-jlcpcb-v3.csv / LCSC C174064). PCB footprint pads are an exact copy of the Gerber_TopLayer.GTL flashes from gerber-pcb-detection-v3.zip (three 0.7mm x 1.25mm pads, 1.9mm/2.5mm SOT-23-3 pitch). Pin numbering (1/2/3) follows physical pad position only - the VCC/GND/OUT mapping was not confirmed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
  XH-3A Connector, DATA/-/+ (detection PCB v3): 3-pin JST-XH 2.5mm through-hole connector, designator "DATA/-/+" on the target-detection PCB (bom-jlcpcb-v3.csv / LCSC C2316) - carries the OH37 output signal plus power to the Pro Micro (see cablage-pro-micro.fzz). PCB footprint pads are an exact copy of the Gerber pad flashes and Drill_PTH_Through.DRL from gerber-pcb-detection-v3.zip (1.8mm pads / 1.0mm drill, 2.5mm pitch). Pin order (DATA,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
